// Logisim project SUBR CIRCUITS.circ as structural Verilog: 1 circuit, main circuit main
module main (
  input  A,
  input  B,
  input  Bin,
  input  A_2,
  input  B_2
);

  wire and_1_out, and_2_out, and_3_out, and_4_out, not_1_out, not_2_out, or_1_out, undriven, undriven_2,
       undriven_3, xor_1_out, xor_2_out, xor_3_out;

  xor xor_1 (xor_1_out, A_2, B_2);
  not not_1 (not_1_out, undriven);
  and and_1 (and_1_out, not_1_out, B_2);
  xor xor_2 (xor_2_out, A, B);
  not not_2 (not_2_out, A);
  LED led_1 (.in(xor_2_out));
  and and_2 (and_2_out, undriven_3, not_1_out);
  and and_3 (and_3_out, undriven_2, B_2);
  and and_4 (and_4_out, not_2_out, B);
  LED led_2 (.in(and_4_out));
  xor xor_3 (xor_3_out, xor_1_out, Bin);
  LED led_3 (.in(xor_3_out));
  or or_1 (or_1_out, and_2_out, and_3_out, and_1_out);
  LED led_4 (.in(or_1_out));

  // Notes on the sheet:
  //   HALF SUBR
  //   D
  //   FULL SUBR
  //   Bo
  //   D
  //   Bo
endmodule
